# Fritzing sketch Carrinho (saved by Fritzing 0.9.3b)
breadboards: 1

parts:
  Componente1 = Arduino Nano (Rev3.0)
  Componente2 = NRF24L01
  M1 = DC Motor  # not connected
  M2 = DC Motor  # not connected

nets:
  N1: Componente1.D7, Componente2.CE
  N2: Componente1.D8, Componente2.CSN
  N3: Componente1.D11/MOSI, Componente2.MOSI
  N4: Componente1.D12/MISO, Componente2.MISO
  3V3: Componente1.3V3, Componente2.VCC
  N5: Componente1.D13/SCK, Componente2.SCK
